# Fritzing sketch Dht11 (saved by Fritzing 0.9.3b)

parts:
  Raspberry_Pi_1 = Raspberry Pi 3 [part_number=RPI-3-V1.2]
  DHT11_1 = DHT11 module

nets:
  N1: Raspberry_Pi_1.GPIO27, DHT11_1.DATA
  GND: Raspberry_Pi_1.GND, DHT11_1.GND
  5V: Raspberry_Pi_1.5V, DHT11_1.VCC

custom parts:
  DHT11 module: DHT11 black pcb module
