# Fritzing sketch Nivel de agua (saved by Fritzing 0.9.3b)

parts:
  Raspberry_Pi_1 = Raspberry Pi 3 [part_number=RPI-3-V1.2]
  Water_Level_Sensor1 = Water Level Sensor

nets:
  N1: Raspberry_Pi_1.GPIO17, Water_Level_Sensor1.SIG
  GND: Raspberry_Pi_1.GND, Water_Level_Sensor1.GND
  5V: Raspberry_Pi_1.5V, Water_Level_Sensor1.VCC

custom parts:
  Water Level Sensor: A water level sensor. This sensor operates at 3V to 5V. The Sig (signal) pin outputs an analogue signal that is in proportion to the amount of water in contact with the sensor.
