# Fritzing sketch Proj_Comp (saved by Fritzing 0.9.3b)

parts:
  Raspberry_Pi_1 = Raspberry Pi 3 [part_number=RPI-3-V1.2]
  DHT11_1 = DHT11 module
  Water_Level_Sensor1 = Water Level Sensor
  Mod1 = KY-017 Mercury Tilt Switch [package="Breakout board"]

nets:
  3V3: Raspberry_Pi_1.3v3, Mod1.Vin
  GND: Raspberry_Pi_1.GND, DHT11_1.GND, Water_Level_Sensor1.GND, Mod1.-
  N1: Raspberry_Pi_1.GPIO17, Water_Level_Sensor1.SIG
  N2: Raspberry_Pi_1.GPIO27, DHT11_1.DATA
  N3: Raspberry_Pi_1.GPIO22, Mod1.S
  VCC: Raspberry_Pi_1.5V, DHT11_1.VCC, Water_Level_Sensor1.VCC

custom parts:
  DHT11 module: DHT11 black pcb module
  Water Level Sensor: A water level sensor. This sensor operates at 3V to 5V. The Sig (signal) pin outputs an analogue signal that is in proportion to the amount of water in contact with the sensor.
  KY-017 Mercury Tilt Switch: KY-017 mercury tilt switch module, it uses a small mercury ball that completes the circuit when you tilt the module.
