# Fritzing sketch ky 017 (saved by Fritzing 0.9.3b)

parts:
  Raspberry_Pi_1 = Raspberry Pi 3 [part_number=RPI-3-V1.2]
  Mod1 = KY-017 Mercury Tilt Switch [package="Breakout board"]

nets:
  3V3: Raspberry_Pi_1.3v3, Mod1.Vin
  N1: Raspberry_Pi_1.GND, Mod1.-
  N2: Raspberry_Pi_1.GPIO22, Mod1.S

custom parts:
  KY-017 Mercury Tilt Switch: KY-017 mercury tilt switch module, it uses a small mercury ball that completes the circuit when you tilt the module.
