# Fritzing sketch Raspberry Pi 3 dht11 (saved by Fritzing 0.9.3b)
breadboards: 1

parts:
  DHT1 = DHT11 Humitidy and Temperature Sensor
  Raspberry_Pi_1 = Raspberry Pi 3 [part_number=RPI-3-V1.2]
  J1 = T Cobbler Plus
  Componente1 = Adafruit BMP180
  SEN1 = Pulse Sensor [package=SIP]

nets:
  N1: DHT1.VDD, J1.5.0V#1
  N2: DHT1.DATA, J1.#23
  N3: DHT1.GND, J1.GND#33
  3V3: Raspberry_Pi_1.3v3, Raspberry_Pi_1.3V3, J1.3.3V#41, J1.3.3V#57
  N4: Raspberry_Pi_1.GPIO2, J1.GPIO_2
  N5: Raspberry_Pi_1.GPIO3, J1.GPIO_3
  N6: Raspberry_Pi_1.GPIO4, J1.GPIO_4
  N7: Raspberry_Pi_1.GND, J1.GND#46, J1.GND#49, J1.GND#54, J1.GND#60, J1.GND#65, J1.GND#70, J1.GND#74, J1.GND#79
  N8: Raspberry_Pi_1.GPIO17, J1.GPIO_17
  N9: Raspberry_Pi_1.GPIO27, J1.GPIO_27
  N10: Raspberry_Pi_1.GPIO22, J1.GPIO_22
  N11: Raspberry_Pi_1.GPIO10, J1.GPIO_10
  N12: Raspberry_Pi_1.GPIO9, J1.GPIO_9
  N13: Raspberry_Pi_1.GPIO11, J1.GPIO_11
  N14: Raspberry_Pi_1.ID_SD, J1.ID_SD
  N15: Raspberry_Pi_1.GPIO5, J1.GPIO_5
  N16: Raspberry_Pi_1.GPIO6, J1.GPIO_6
  N17: Raspberry_Pi_1.GPIO13, J1.GPIO_13
  N18: Raspberry_Pi_1.GPIO19, J1.GPIO_19
  N19: Raspberry_Pi_1.GPIO26, J1.GPIO_26
  N20: Raspberry_Pi_1.GPIO21, J1.GPIO_21
  N21: Raspberry_Pi_1.GPIO20, J1.GPIO_20
  N22: Raspberry_Pi_1.GPIO16, J1.GPIO_16
  N23: Raspberry_Pi_1.GPIO12, J1.GPIO_12
  N24: Raspberry_Pi_1.ID_SC, J1.ID_SC
  N25: Raspberry_Pi_1.GPIO7, J1.GPIO_7
  N26: Raspberry_Pi_1.GPIO8, J1.GPIO_8
  N27: Raspberry_Pi_1.GPIO25, J1.GPIO_25
  N28: Raspberry_Pi_1.GPIO24, J1.GPIO_24
  N29: Raspberry_Pi_1.GPIO23, J1.GPIO_23
  N30: Raspberry_Pi_1.GPIO18, J1.GPIO_18
  N31: Raspberry_Pi_1.GPIO15, J1.GPIO_15
  N32: Raspberry_Pi_1.GPIO14, J1.GPIO_14
  5V: Raspberry_Pi_1.5V, J1.5V
  3V3_2: J1.3V3, SEN1.Vcc
  N33: J1.5.0V#3, Componente1.+5V
  N34: J1.GND#5, Componente1.GND
  N35: J1.#24, Componente1.SDA
  N36: J1.#26, SEN1.Signal
  N37: J1.GND#38, SEN1.GND

custom parts:
  DHT11 Humitidy and Temperature Sensor: DHT11 Humidity and Temperature Sensor
  T Cobbler Plus: The T-Cobbler Plus is an add on prototyping board from Adafruit specifically designed for the Raspberry Pi B+ that can break out all those tasty power, GPIO, I2C and SPI pins from the 40-pin header onto a solderless breadboard. This set will make "cobbling together" prototypes with the Pi super easy. The T-Cobbler Plus can plug into any solderless breadboard.
  Adafruit BMP180: This precision sensor from Bosch is the best low-cost sensing solution for measuring barometric pressure and temperature. Because pressure changes with altitude you can also use it as an altimeter! The sensor is soldered onto a PCB with a 3.3V regulator, I2C level shifter and pull-up resistors on the I2C pins. The BMP180 is the next-generation of sensors from Bosch, and replaces the BMP085.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
  Pulse Sensor: Pulse Sensor Optical Heart Rate Monitor for Arduino and other microcontrollers
